# Fritzing sketch trinket-snes (saved by Fritzing 0.9.3b)

parts:
  IC1 = IC, SIP package, 5 pins [chip_label=SNES]
  Part1 = Adafruit Trinket 5V

nets:
  N1: IC1.pin1, Part1.+5V
  N2: IC1.pin2, Part1.#2
  N3: IC1.pin3, Part1.#1
  N4: IC1.pin4, Part1.#0
  N5: IC1.pin5, Part1.GND

custom parts:
  Adafruit Trinket 5V: Trinket may be small, but do not be fooled by its size! It's a tiny microcontroller board, built around the Atmel ATtiny85, a little chip with a lot of power. We wanted to design a microcontroller board that was small enough to fit into any project, and low cost enough to use without hesitation. Perfect for when you don't want to give up your expensive dev-board and you aren't willing to take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
